// Logisim project ALU_Design_main.circ as structural Verilog: 16 circuits, main circuit ALU32
module ALU32 (
  input  [31:0] A,
  input  [31:0] B,
  input  [3:0] Op,
  input  [4:0] Sa,
  output [31:0] C,
  output V
);

  wire [31:0] alu_compare_1_c, alu_compute_1_c, alu_logic_1_c, alu_shift_1_c;

  ALU_Logic alu_logic_1 (.A(A), .B(B), .Op(Op), .C(alu_logic_1_c));
  ALU_Compare alu_compare_1 (.A(A), .B(B), .Op(Op), .C(alu_compare_1_c));
  ALU_Compute alu_compute_1 (.B(B), .A(A), .Op(Op), .V(V), .C(alu_compute_1_c));
  ALU_Shift alu_shift_1 (.B(B), .Op(Op), .Sa(Sa), .C(alu_shift_1_c));
  assign C = alu_logic_1_c | alu_compare_1_c | alu_compute_1_c | alu_shift_1_c;  // OR_Gate or_1, 32 bits wide
endmodule

module ALU_Logic (
  input  [31:0] A,
  input  [31:0] B,
  input  [3:0] Op,
  output [31:0] C
);

  wire and_2_out, and_3_out, or_2_out;
  wire [31:0] and_1_out, nor_1_out, or_1_out, xor_1_out;

  assign and_1_out = A & B;  // AND_Gate and_1, 32 bits wide
  assign or_1_out = A | B;  // OR_Gate or_1, 32 bits wide
  assign xor_1_out = A ^ B;  // XOR_Gate xor_1, 32 bits wide
  assign nor_1_out = ~(A | B);  // NOR_Gate nor_1, 32 bits wide
  and and_2 (and_2_out, Op[3], ~Op[2], Op[1]);  // AND_Gate
  and and_3 (and_3_out, ~Op[3], Op[2], ~Op[1]);  // AND_Gate
  or or_2 (or_2_out, and_2_out, and_3_out);
  Multiplexer #(.select(2), .width(32)) multiplexer_1 (
    .in0(and_1_out), .in1(or_1_out), .in2(xor_1_out), .in3(nor_1_out), .out(C), .sel(Op[1:0]), .en(or_2_out));

  // Notes on the sheet:
  //   Op wrong -> output 0 to C
endmodule

module ALU_Compare (
  input  [31:0] A,
  input  [31:0] B,
  input  [3:0] Op,
  output [31:0] C
);

  wire and_1_out, and_4_out, and_5_out, and_6_out, not_2_out, not_3_out, xnor_2_out;
  wire [1:0] and_2_out, and_3_out;
  wire [31:0] bit_extender_1_out, bit_extender_2_out, bit_extender_3_out, bit_extender_4_out, not_1_out,
       xnor_1_out;

  assign not_1_out = ~A;  // NOT_Gate not_1, 32 bits wide
  assign xnor_1_out = ~(B ^ A);  // XNOR_Gate xnor_1, 32 bits wide
  xnor xnor_2 (xnor_2_out, Op[2], Op[1]);
  and and_1 (and_1_out, xnor_2_out, Op[3]);
  assign and_2_out = not_1_out[31:30] & not_1_out[29:28] & not_1_out[27:26] & not_1_out[25:24] & not_1_out[23:22] & not_1_out[21:20] & not_1_out[19:18] & not_1_out[17:16] & not_1_out[15:14] & not_1_out[13:12] & not_1_out[11:10] & not_1_out[9:8] & not_1_out[7:6] & not_1_out[5:4] & not_1_out[3:2] & not_1_out[1:0];  // AND_Gate and_2, 2 bits wide
  assign and_3_out = xnor_1_out[31:30] & xnor_1_out[29:28] & xnor_1_out[27:26] & xnor_1_out[25:24] & xnor_1_out[23:22] & xnor_1_out[21:20] & xnor_1_out[19:18] & xnor_1_out[17:16] & xnor_1_out[15:14] & xnor_1_out[13:12] & xnor_1_out[11:10] & xnor_1_out[9:8] & xnor_1_out[7:6] & xnor_1_out[5:4] & xnor_1_out[3:2] & xnor_1_out[1:0];  // AND_Gate and_3, 2 bits wide
  and and_4 (and_4_out, and_2_out[0], and_2_out[1]);
  and and_5 (and_5_out, and_3_out[0], and_3_out[1]);
  and and_6 (and_6_out, ~A[31], ~and_4_out);  // AND_Gate
  not not_2 (not_2_out, and_5_out);
  not not_3 (not_3_out, and_6_out);
  assign bit_extender_1_out = {{31{1'b0}}, not_2_out};  // Bit_Extender bit_extender_1
  assign bit_extender_2_out = {{31{1'b0}}, and_5_out};  // Bit_Extender bit_extender_2
  assign bit_extender_3_out = {{31{1'b0}}, not_3_out};  // Bit_Extender bit_extender_3
  assign bit_extender_4_out = {{31{1'b0}}, and_6_out};  // Bit_Extender bit_extender_4
  Multiplexer #(.select(2), .width(32)) multiplexer_1 (
    .in0(bit_extender_1_out), .in1(bit_extender_2_out), .in2(bit_extender_3_out), .in3(bit_extender_4_out),
    .out(C), .sel(Op[1:0]), .en(and_1_out));

  // Notes on the sheet:
  //   If Op wrong, output 0 to C
endmodule

module ALU_Compute (
  input  [31:0] B,
  input  [31:0] A,
  input  [3:0] Op,
  output V,
  output [31:0] C
);

  wire and_1_out, and_2_out;
  wire [31:0] and_3_out, and_4_out, bit_extender_1_out, multiplexer_1_out, not_1_out;

  Multiplexer #(.width(32), .enable("false")) multiplexer_1 (
    .in0(B), .in1(not_1_out), .out(multiplexer_1_out), .sel(Op[2]));
  assign not_1_out = ~B;  // NOT_Gate not_1, 32 bits wide
  and and_1 (and_1_out, Op[1], ~Op[3]);  // AND_Gate
  assign bit_extender_1_out = {{31{and_1_out}}, and_1_out};  // Bit_Extender bit_extender_1
  and and_2 (and_2_out, and_1_out, Op[2]);
  assign and_3_out = multiplexer_1_out & bit_extender_1_out;  // AND_Gate and_3, 32 bits wide
  assign and_4_out = bit_extender_1_out & A;  // AND_Gate and_4, 32 bits wide
  Add32 add32_1 (.B(and_3_out), .A(and_4_out), .Cin(and_2_out), .V(V), .C(C));

  // Notes on the sheet:
  //   Choose B or -B
  //   If Op wrong, input 0
  //   If Op wrong output C to Cin
endmodule

module ALU_Shift (
  input  [31:0] B,
  input  [3:0] Op,
  input  [4:0] Sa,
  output [31:0] C
);

  wire and_1_out, and_2_out, and_3_out, and_4_out, or_1_out;
  wire [4:0] and_5_out, bit_extender_1_out;
  wire [31:0] leftshift32_1_c, multiplexer_1_out, reverse_1_bout, reverse_2_bout;

  Reverse reverse_1 (.B(B), .Bout(reverse_1_bout));
  and and_1 (and_1_out, ~Op[1], ~Op[2], ~Op[3]);  // AND_Gate
  and and_2 (and_2_out, ~Op[1], Op[2], Op[3]);  // AND_Gate
  Multiplexer #(.width(32)) multiplexer_1 (
    .in0(B), .in1(reverse_1_bout), .out(multiplexer_1_out), .sel(Op[3]), .en(or_1_out));
  and and_3 (and_3_out, B[31], Op[0]);
  or or_1 (or_1_out, and_1_out, and_2_out);
  and and_4 (and_4_out, and_3_out, Op[3]);
  assign bit_extender_1_out = {{4{or_1_out}}, or_1_out};  // Bit_Extender bit_extender_1
  assign and_5_out = bit_extender_1_out & Sa;  // AND_Gate and_5, 5 bits wide
  LeftShift32 leftshift32_1 (.B(multiplexer_1_out), .Cin(and_4_out), .Sa(and_5_out), .C(leftshift32_1_c));
  Reverse reverse_2 (.B(leftshift32_1_c), .Bout(reverse_2_bout));
  Multiplexer #(.width(32), .enable("false")) multiplexer_2 (
    .in0(leftshift32_1_c), .in1(reverse_2_bout), .out(C), .sel(Op[3]));

  // Notes on the sheet:
  //   Reverse or not 
  //   If Op wrong, output 0 to Sa
  //   Reverse or not 
  //   If Op wrong, output 0 to C
endmodule

module LeftShift32 (
  input  [31:0] B,
  input  Cin,
  input  [4:0] Sa,
  output [31:0] C
);

  wire [31:0] leftshift1_1_c, leftshift2_1_c, leftshift4_1_c, leftshift8_1_c, leftshift16_1_c,
       multiplexer_1_out, multiplexer_2_out, multiplexer_3_out, multiplexer_4_out;

  LeftShift1 leftshift1_1 (.Cin(Cin), .B(B), .C(leftshift1_1_c));
  Multiplexer #(.width(32), .enable("false")) multiplexer_1 (
    .in0(B), .in1(leftshift1_1_c), .out(multiplexer_1_out), .sel(Sa[0]));
  LeftShift2 leftshift2_1 (.Cin(Cin), .B(multiplexer_1_out), .C(leftshift2_1_c));
  Multiplexer #(.width(32), .enable("false")) multiplexer_2 (
    .in0(multiplexer_1_out), .in1(leftshift2_1_c), .out(multiplexer_2_out), .sel(Sa[1]));
  LeftShift4 leftshift4_1 (.Cin(Cin), .B(multiplexer_2_out), .C(leftshift4_1_c));
  Multiplexer #(.width(32), .enable("false")) multiplexer_3 (
    .in0(multiplexer_2_out), .in1(leftshift4_1_c), .out(multiplexer_3_out), .sel(Sa[2]));
  LeftShift8 leftshift8_1 (.Cin(Cin), .B(multiplexer_3_out), .C(leftshift8_1_c));
  Multiplexer #(.width(32), .enable("false")) multiplexer_4 (
    .in0(multiplexer_3_out), .in1(leftshift8_1_c), .out(multiplexer_4_out), .sel(Sa[3]));
  Multiplexer #(.width(32), .enable("false")) multiplexer_5 (
    .in0(multiplexer_4_out), .in1(leftshift16_1_c), .out(C), .sel(Sa[4]));
  LeftShift16 leftshift16_1 (.Cin(Cin), .B(multiplexer_4_out), .C(leftshift16_1_c));

  // Notes on the sheet:
  //   Do not delete or rename any of the input or output pins, and do not add any other pins.
  //   (It's fine to move them around, though)
endmodule

module Add32 (
  input  [31:0] B,
  input  [31:0] A,
  input  Cin,
  output V,
  output [31:0] C
);

  wire add16_1_cout, add16_2_cout, add16_2_v_overflow;

  Add16 add16_1 (.B(B[15:0]), .A(A[15:0]), .Cin(Cin), .Cout(add16_1_cout), .C(C[15:0]));  // open: V_Overflow
  Add16 add16_2 (
    .B(B[31:16]), .A(A[31:16]), .Cin(add16_1_cout), .Cout(add16_2_cout), .V_Overflow(add16_2_v_overflow),
    .C(C[31:16]));
  xor xor_1 (V, add16_2_cout, add16_2_v_overflow);
endmodule

module LeftShift1 (
  input  Cin,
  input  [31:0] B,
  output [31:0] C
);


  assign C = {B[30:0], Cin};
endmodule

module LeftShift2 (
  input  Cin,
  input  [31:0] B,
  output [31:0] C
);

  wire [31:0] leftshift1_1_c;

  LeftShift1 leftshift1_1 (.Cin(Cin), .B(B), .C(leftshift1_1_c));
  LeftShift1 leftshift1_2 (.Cin(Cin), .B(leftshift1_1_c), .C(C));
endmodule

module LeftShift4 (
  input  Cin,
  input  [31:0] B,
  output [31:0] C
);

  wire [31:0] leftshift2_1_c;

  LeftShift2 leftshift2_1 (.Cin(Cin), .B(B), .C(leftshift2_1_c));
  LeftShift2 leftshift2_2 (.Cin(Cin), .B(leftshift2_1_c), .C(C));
endmodule

module LeftShift8 (
  input  Cin,
  input  [31:0] B,
  output [31:0] C
);

  wire [31:0] leftshift4_1_c;

  LeftShift4 leftshift4_1 (.Cin(Cin), .B(B), .C(leftshift4_1_c));
  LeftShift4 leftshift4_2 (.Cin(Cin), .B(leftshift4_1_c), .C(C));
endmodule

module LeftShift16 (
  input  Cin,
  input  [31:0] B,
  output [31:0] C
);

  wire [31:0] leftshift8_1_c;

  LeftShift8 leftshift8_1 (.Cin(Cin), .B(B), .C(leftshift8_1_c));
  LeftShift8 leftshift8_2 (.Cin(Cin), .B(leftshift8_1_c), .C(C));
endmodule

module Add1 (
  input  A,
  input  B,
  input  Cin,
  output S,
  output Cout
);

  wire and_1_out, and_2_out, xor_1_out;

  xor xor_1 (xor_1_out, A, B);
  and and_1 (and_1_out, xor_1_out, Cin);
  and and_2 (and_2_out, A, B);
  xor xor_2 (S, xor_1_out, Cin);
  or or_1 (Cout, and_1_out, and_2_out);
endmodule

module Add4 (
  input  [3:0] B,
  input  [3:0] A,
  input  Cin,
  output Cout,
  output V_Overflow,
  output [3:0] C
);

  wire add1_1_cout, add1_2_cout;

  Add1 add1_1 (.A(A[0]), .B(B[0]), .Cin(Cin), .S(C[0]), .Cout(add1_1_cout));
  Add1 add1_2 (.A(A[1]), .B(B[1]), .Cin(add1_1_cout), .S(C[1]), .Cout(add1_2_cout));
  Add1 add1_3 (.A(A[2]), .B(B[2]), .Cin(add1_2_cout), .S(C[2]), .Cout(V_Overflow));
  Add1 add1_4 (.A(A[3]), .B(B[3]), .Cin(V_Overflow), .S(C[3]), .Cout(Cout));
endmodule

module Add16 (
  input  [15:0] B,
  input  [15:0] A,
  input  Cin,
  output Cout,
  output V_Overflow,
  output [15:0] C
);

  wire add4_1_cout, add4_2_cout, add4_3_cout;

  Add4 add4_1 (.B(B[3:0]), .A(A[3:0]), .Cin(Cin), .Cout(add4_1_cout), .C(C[3:0]));  // open: V_Overflow
  Add4 add4_2 (.B(B[7:4]), .A(A[7:4]), .Cin(add4_1_cout), .Cout(add4_2_cout), .C(C[7:4]));  // open: V_Overflow
  Add4 add4_3 (.B(B[11:8]), .A(A[11:8]), .Cin(add4_2_cout), .Cout(add4_3_cout), .C(C[11:8]));  // open: V_Overflow
  Add4 add4_4 (.B(B[15:12]), .A(A[15:12]), .Cin(add4_3_cout), .Cout(Cout), .V_Overflow(V_Overflow), .C(C[15:12]));
endmodule

module Reverse (
  input  [31:0] B,
  output [31:0] Bout
);


  assign Bout = {B[0], B[1], B[2], B[3], B[4], B[5], B[6], B[7], B[8], B[9], B[10], B[11], B[12], B[13], B[14], B[15], B[16], B[17], B[18], B[19], B[20], B[21], B[22], B[23], B[24], B[25], B[26], B[27], B[28], B[29], B[30], B[31]};

  // Notes on the sheet:
  //   Reverse Value of B
endmodule
